# Fritzing sketch aircraft_launching (saved by Fritzing 0.9.3b)
breadboards: 1

parts:
  R4 = Resistor [tolerance=±5% resistance=330 package=THT]
  S1 = Pushbutton [package=THT]
  S2 = Pushbutton [package=THT]
  R3 = Resistor [tolerance=±5% resistance=330 package=THT]
  Arduino_Mega_(2560) = Arduino Mega 2560 (Rev3)
  LED2 = LED - 3mm [color="Blue (470nm)" package="3 mm [THT]"]
  LED1 = LED - 3mm [color="Blue (470nm)" package="3 mm [THT]"]
  R1 = Resistor [tolerance=±5% resistance=1k package=THT]
  R2 = Resistor [tolerance=±5% resistance=1k package=THT]
  MOTOR1 = 28BYJ-48 Stepper Motor
  X1 = X113647 Stepper Driver Board [package=board]
  X2 = X113647 Stepper Driver Board [package=board]
  MOTOR2 = 28BYJ-48 Stepper Motor
  M1 = DC Motor
  M2 = DC Motor
  S3 = Toggle Switch [package=THT]
  VCC3 = 4 x AAA Battery Mount
  VCC4 = 4 x AAA Battery Mount
  VCC1 = 4 x AAA Battery Mount
  VCC2 = 4 x AAA Battery Mount

nets:
  N1: R4.Pin_0, LED2.anode
  N2: R4.Pin_1, Arduino_Mega_(2560).D24
  N3: S1.leg0, S2.leg0, Arduino_Mega_(2560).5V
  N4: S1.leg1, Arduino_Mega_(2560).D23, R1.Pin_1
  N5: S2.leg1, Arduino_Mega_(2560).D22, R2.Pin_1
  N6: R3.Pin_0, LED1.anode
  N7: R3.Pin_1, Arduino_Mega_(2560).D25
  GND: Arduino_Mega_(2560).GND, LED2.cathode, LED1.cathode, R1.Pin_0, R2.Pin_0, X1.GND, X2.GND, VCC3.-, VCC2.-
  N8: Arduino_Mega_(2560).D11_PWM, X1.IN4
  N9: Arduino_Mega_(2560).D10_PWM, X1.IN3
  N10: Arduino_Mega_(2560).D9_PWM, X1.IN2
  N11: Arduino_Mega_(2560).D8_PWM, X1.IN1
  N12: Arduino_Mega_(2560).D50, X2.IN1
  N13: Arduino_Mega_(2560).D51, X2.IN2
  N14: Arduino_Mega_(2560).D52, X2.IN3
  N15: Arduino_Mega_(2560).D53, X2.IN4
  N16: MOTOR1.BLUE, X1.BLUE
  N17: MOTOR1.PINK, X1.PINK
  N18: MOTOR1.RED, X1.RED
  N19: MOTOR1.ORANGE, X1.ORANGE
  N20: MOTOR1.YELLOW, X1.YELLOW
  N21: X1.+V, VCC3.+
  N22: X2.+V, VCC1.+
  N23: X2.BLUE, MOTOR2.BLUE
  N24: X2.PINK, MOTOR2.PINK
  N25: X2.YELLOW, MOTOR2.YELLOW
  N26: X2.ORANGE, MOTOR2.ORANGE
  N27: X2.RED, MOTOR2.RED
  N28: M1.pin_1, M2.pin_1, VCC4.-
  N29: M1.pin_2, M2.pin_2, S3.L2
  N30: S3.COM, VCC4.+
  N31: VCC1.-, VCC2.+

notes:
  5V for the 5V Stepper Motor
  10V for the 12V Stepper Motor
  5V for the DC Motors

custom parts:
  28BYJ-48 Stepper Motor: 28BYJ-48 gear-reduction stepper motor (small)
  X113647 Stepper Driver Board: A common stepper motor driver board based on ULN2003APG darlington array

// code stored in the sketch: aircraft_launching.ino
//motor 1
const int IN1_M1 = 8;      // pin digital 8 de Arduino a IN1 de modulo controlador
const int IN2_M1 = 9;      // pin digital 9 de Arduino a IN2 de modulo controlador
const int IN3_M1 = 10;     // pin digital 10 de Arduino a IN3 de modulo controlador
const int IN4_M1 = 11;     // pin digital 11 de Arduino a IN4 de modulo controlador

//motor 2
const int IN1_M2 = 50;      // pin digital 8 de Arduino a IN1 de modulo controlador
const int IN2_M2 = 51;      // pin digital 9 de Arduino a IN2 de modulo controlador
const int IN3_M2 = 52;     // pin digital 10 de Arduino a IN3 de modulo controlador
const int IN4_M2 = 53;     // pin digital 11 de Arduino a IN4 de modulo controlador

const int demora = 10;      // demora entre pasos, no debe ser menor a 10 ms.

const int BOT1 = 22;
const int BOT2 = 23;
const int LED1 = 24;
const int LED2 = 25;


void setup()
{
  Serial.begin(9600);
  
  pinMode(IN1_M1, OUTPUT);   // todos los pines como salida o entrada
  pinMode(IN2_M1, OUTPUT);
  pinMode(IN3_M1, OUTPUT);
  pinMode(IN4_M1, OUTPUT);
  
  pinMode(IN1_M2, OUTPUT);
  pinMode(IN2_M2, OUTPUT);
  pinMode(IN3_M2, OUTPUT);
  pinMode(IN4_M2, OUTPUT);

  pinMode(BOT1,INPUT);
  pinMode(BOT2,INPUT);
  
  pinMode(LED1,OUTPUT);
  pinMode(LED2,OUTPUT);
}

void loop()
{
  if(digitalRead(BOT1))
  {
    Serial.print("subiendo...\n");
    digitalWrite(LED1,1);
    digitalWrite(LED2,0);
    giroSub(1);
  }
  else if(digitalRead(BOT2))
  {
    Serial.print("bajando...\n");
    digitalWrite(LED1,0);
    digitalWrite(LED2,1);
    giroBaj(1);
  }
  else
  {
    digitalWrite(LED1,0);
    digitalWrite(LED2,0);
  }
  delay(20);
}

void giroSub(int a)
{
  for (int i = 0; i < a; i++)
  {
    digitalWrite(IN1_M1, HIGH);  // paso 1 
    digitalWrite(IN1_M2, HIGH);
    digitalWrite(IN2_M1, LOW);
    digitalWrite(IN2_M2, LOW);
    digitalWrite(IN3_M1, LOW);
    digitalWrite(IN3_M2, LOW);
    digitalWrite(IN4_M1, LOW);
    digitalWrite(IN4_M2, LOW);
    delay(demora);

    digitalWrite(IN1_M1, LOW); // paso 2
    digitalWrite(IN1_M2, LOW);
    digitalWrite(IN2_M1, HIGH);
    digitalWrite(IN2_M2, HIGH);
    digitalWrite(IN3_M1, LOW);
    digitalWrite(IN3_M2, LOW);
    digitalWrite(IN4_M1, LOW);
    digitalWrite(IN4_M2, LOW);
    delay(demora);

    digitalWrite(IN1_M1, LOW); // paso 3
    digitalWrite(IN1_M2, LOW);
    digitalWrite(IN2_M1, LOW);
    digitalWrite(IN2_M2, LOW);
    digitalWrite(IN3_M1, HIGH);
    digitalWrite(IN3_M2, HIGH);
    digitalWrite(IN4_M1, LOW);
    digitalWrite(IN4_M2, LOW);
    delay(demora);

    digitalWrite(IN1_M1, LOW); // paso 4
    digitalWrite(IN1_M2, LOW);
    digitalWrite(IN2_M1, LOW);
    digitalWrite(IN2_M2, LOW);
    digitalWrite(IN3_M1, LOW);
    digitalWrite(IN3_M2, LOW);
    digitalWrite(IN4_M1, HIGH);
    digitalWrite(IN4_M2, HIGH);
    delay(demora);

    digitalWrite(IN1_M1, LOW); // detiene por 0.2 seg.
    digitalWrite(IN1_M2, LOW);
    digitalWrite(IN2_M1, LOW);
    digitalWrite(IN2_M2, LOW);
    digitalWrite(IN3_M1, LOW);
    digitalWrite(IN3_M2, LOW);
    digitalWrite(IN4_M1, LOW);
    digitalWrite(IN4_M2, LOW);
    delay(200);
  }
}

//________________________________________________________________
//________________________________________________________________

void giroSub(int a)
{
  for (int i = 0; i < a; i++)
  {
    digitalWrite(IN1_M1, LOW); // paso 4
    digitalWrite(IN1_M2, LOW);
    digitalWrite(IN2_M1, LOW);
    digitalWrite(IN2_M2, LOW);
    digitalWrite(IN3_M1, LOW);
    digitalWrite(IN3_M2, LOW);
    digitalWrite(IN4_M1, HIGH);
    digitalWrite(IN4_M2, HIGH);
    delay(demora);
    
    digitalWrite(IN1_M1, LOW); // paso 3
    digitalWrite(IN1_M2, LOW);
    digitalWrite(IN2_M1, LOW);
    digitalWrite(IN2_M2, LOW);
    digitalWrite(IN3_M1, HIGH);
    digitalWrite(IN3_M2, HIGH);
    digitalWrite(IN4_M1, LOW);
    digitalWrite(IN4_M2, LOW);
    delay(demora);

    digitalWrite(IN1_M1, LOW); // paso 2
    digitalWrite(IN1_M2, LOW);
    digitalWrite(IN2_M1, HIGH);
    digitalWrite(IN2_M2, HIGH);
    digitalWrite(IN3_M1, LOW);
    digitalWrite(IN3_M2, LOW);
    digitalWrite(IN4_M1, LOW);
    digitalWrite(IN4_M2, LOW);
    delay(demora);
    
    digitalWrite(IN1_M1, HIGH);  // paso 1 
    digitalWrite(IN1_M2, HIGH);
    digitalWrite(IN2_M1, LOW);
    digitalWrite(IN2_M2, LOW);
    digitalWrite(IN3_M1, LOW);
    digitalWrite(IN3_M2, LOW);
    digitalWrite(IN4_M1, LOW);
    digitalWrite(IN4_M2, LOW);
    delay(demora);
    
    digitalWrite(IN1_M1, LOW); // detiene por 0.2 seg.
    digitalWrite(IN1_M2, LOW);
    digitalWrite(IN2_M1, LOW);
    digitalWrite(IN2_M2, LOW);
    digitalWrite(IN3_M1, LOW);
    digitalWrite(IN3_M2, LOW);
    digitalWrite(IN4_M1, LOW);
    digitalWrite(IN4_M2, LOW);
    delay(200);
  }
}

// code stored in the sketch: aircraft_launching.ino.ino
//motor 1
const int IN1_M1 = 8;      // pin digital 8 de Arduino a IN1 de modulo controlador
const int IN2_M1 = 9;      // pin digital 9 de Arduino a IN2 de modulo controlador
const int IN3_M1 = 10;     // pin digital 10 de Arduino a IN3 de modulo controlador
const int IN4_M1 = 11;     // pin digital 11 de Arduino a IN4 de modulo controlador

//motor 2
const int IN1_M2 = 50;      // pin digital 8 de Arduino a IN1 de modulo controlador
const int IN2_M2 = 51;      // pin digital 9 de Arduino a IN2 de modulo controlador
const int IN3_M2 = 52;     // pin digital 10 de Arduino a IN3 de modulo controlador
const int IN4_M2 = 53;     // pin digital 11 de Arduino a IN4 de modulo controlador

const int demora = 10;      // demora entre pasos, no debe ser menor a 10 ms.

const int BOT1 = 22;
const int BOT2 = 23;
const int LED1 = 24;
const int LED2 = 25;


void setup()
{
  Serial.begin(9600);
  
  pinMode(IN1_M1, OUTPUT);   // todos los pines como salida o entrada
  pinMode(IN2_M1, OUTPUT);
  pinMode(IN3_M1, OUTPUT);
  pinMode(IN4_M1, OUTPUT);
  
  pinMode(IN1_M2, OUTPUT);
  pinMode(IN2_M2, OUTPUT);
  pinMode(IN3_M2, OUTPUT);
  pinMode(IN4_M2, OUTPUT);

  pinMode(BOT1,INPUT);
  pinMode(BOT2,INPUT);
  
  pinMode(LED1,OUTPUT);
  pinMode(LED2,OUTPUT);
}

void loop()
{
  if(digitalRead(BOT1))
  {
    Serial.print("subiendo...\n");
    digitalWrite(LED1,1);
    digitalWrite(LED2,0);
    giroSub(1);
  }
  else if(digitalRead(BOT2))
  {
    Serial.print("bajando...\n");
    digitalWrite(LED1,0);
    digitalWrite(LED2,1);
    giroBaj(1);
  }
  else
  {
    digitalWrite(LED1,0);
    digitalWrite(LED2,0);
  }
  delay(20);
}

void giroSub(int a)
{
  for (int i = 0; i < a; i++)
  {
    digitalWrite(IN1_M1, HIGH);  // paso 1 
    digitalWrite(IN1_M2, HIGH);
    digitalWrite(IN2_M1, LOW);
    digitalWrite(IN2_M2, LOW);
    digitalWrite(IN3_M1, LOW);
    digitalWrite(IN3_M2, LOW);
    digitalWrite(IN4_M1, LOW);
    digitalWrite(IN4_M2, LOW);
    delay(demora);

    digitalWrite(IN1_M1, LOW); // paso 2
    digitalWrite(IN1_M2, LOW);
    digitalWrite(IN2_M1, HIGH);
    digitalWrite(IN2_M2, HIGH);
    digitalWrite(IN3_M1, LOW);
    digitalWrite(IN3_M2, LOW);
    digitalWrite(IN4_M1, LOW);
    digitalWrite(IN4_M2, LOW);
    delay(demora);

    digitalWrite(IN1_M1, LOW); // paso 3
    digitalWrite(IN1_M2, LOW);
    digitalWrite(IN2_M1, LOW);
    digitalWrite(IN2_M2, LOW);
    digitalWrite(IN3_M1, HIGH);
    digitalWrite(IN3_M2, HIGH);
    digitalWrite(IN4_M1, LOW);
    digitalWrite(IN4_M2, LOW);
    delay(demora);

    digitalWrite(IN1_M1, LOW); // paso 4
    digitalWrite(IN1_M2, LOW);
    digitalWrite(IN2_M1, LOW);
    digitalWrite(IN2_M2, LOW);
    digitalWrite(IN3_M1, LOW);
    digitalWrite(IN3_M2, LOW);
    digitalWrite(IN4_M1, HIGH);
    digitalWrite(IN4_M2, HIGH);
    delay(demora);

    digitalWrite(IN1_M1, LOW); // detiene por 0.2 seg.
    digitalWrite(IN1_M2, LOW);
    digitalWrite(IN2_M1, LOW);
    digitalWrite(IN2_M2, LOW);
    digitalWrite(IN3_M1, LOW);
    digitalWrite(IN3_M2, LOW);
    digitalWrite(IN4_M1, LOW);
    digitalWrite(IN4_M2, LOW);
    delay(200);
  }
}

//________________________________________________________________
//________________________________________________________________

void giroSub(int a)
{
  for (int i = 0; i < a; i++)
  {
    digitalWrite(IN1_M1, LOW); // paso 4
    digitalWrite(IN1_M2, LOW);
    digitalWrite(IN2_M1, LOW);
    digitalWrite(IN2_M2, LOW);
    digitalWrite(IN3_M1, LOW);
    digitalWrite(IN3_M2, LOW);
    digitalWrite(IN4_M1, HIGH);
    digitalWrite(IN4_M2, HIGH);
    delay(demora);
    
    digitalWrite(IN1_M1, LOW); // paso 3
    digitalWrite(IN1_M2, LOW);
    digitalWrite(IN2_M1, LOW);
    digitalWrite(IN2_M2, LOW);
    digitalWrite(IN3_M1, HIGH);
    digitalWrite(IN3_M2, HIGH);
    digitalWrite(IN4_M1, LOW);
    digitalWrite(IN4_M2, LOW);
    delay(demora);

    digitalWrite(IN1_M1, LOW); // paso 2
    digitalWrite(IN1_M2, LOW);
    digitalWrite(IN2_M1, HIGH);
    digitalWrite(IN2_M2, HIGH);
    digitalWrite(IN3_M1, LOW);
    digitalWrite(IN3_M2, LOW);
    digitalWrite(IN4_M1, LOW);
    digitalWrite(IN4_M2, LOW);
    delay(demora);
    
    digitalWrite(IN1_M1, HIGH);  // paso 1 
    digitalWrite(IN1_M2, HIGH);
    digitalWrite(IN2_M1, LOW);
    digitalWrite(IN2_M2, LOW);
    digitalWrite(IN3_M1, LOW);
    digitalWrite(IN3_M2, LOW);
    digitalWrite(IN4_M1, LOW);
    digitalWrite(IN4_M2, LOW);
    delay(demora);
    
    digitalWrite(IN1_M1, LOW); // detiene por 0.2 seg.
    digitalWrite(IN1_M2, LOW);
    digitalWrite(IN2_M1, LOW);
    digitalWrite(IN2_M2, LOW);
    digitalWrite(IN3_M1, LOW);
    digitalWrite(IN3_M2, LOW);
    digitalWrite(IN4_M1, LOW);
    digitalWrite(IN4_M2, LOW);
    delay(200);
  }
}

// code stored in the sketch: AnalogReadSerial2LCD_LED.ino
#include <Wire.h>
#include <LiquidCrystal_I2C.h>

LiquidCrystal_I2C lcd(0x27, 16, 2);   // adress and format LCD

const int analogInPin = A0;           // Analog input pin that the potentiometer is attached to
const int analogOutPin = 9;           // Analog output pin that the LED is attached to

int sensorValue = 0;                  // value read from the pot
int outputValue = 0;                  // value output to the PWM (analog out)

void setup() {
  lcd.init();                         // init LCD
  lcd.backlight();
  lcd.home();
  lcd.setCursor(5, 0);                // place static text
  lcd.print("ADC = ");
  lcd.setCursor(15, 0);
  lcd.print("V");
  lcd.setCursor(0, 1);
  lcd.print("LED : ");
  lcd.setCursor(12, 1);
  lcd.print("%");
  Serial.begin(9600);                 // optional serial monitor
}

void loop() {
  int sensorValue = analogRead(analogInPin);          // read analog A0 en store in sensorValue
  float voltValue = 5.0 / 1024.0 * sensorValue;       // calculate volt at analog A0 and store in voltValue
  float percentValue = sensorValue / 1024.0 * 100.0;  // calculate percentage analog A0 and store in percentValue
  outputValue = map(sensorValue, 0, 1023, 0, 255);    // map analog input to analog output and store in outputValue
  analogWrite(analogOutPin, outputValue);             // write outputValue to analogOutPin

  lcd.setCursor(0, 0);                                // set cursor at deserid position
  leadingZeros(sensorValue, 4);                       // print sensorvalue with number of leading-characters (0 or space as specified in function leadingZeros)
  lcd.setCursor(10, 0);                               // set cursor at deserid position
  lcd.print(voltValue);                               // print voltValue
  lcd.setCursor(6, 1);                                // set cursor at deserid position
  lcd.print(percentValue);                            // print percentValue

  Serial.print("sensor = " );                         // print the results to the serial monitor:
  Serial.print(sensorValue);
  Serial.print("\t output = ");
  Serial.print(outputValue);
  Serial.print("\t procent = ");
  Serial.println(percentValue);

  delay(1000);                                        // set delay
}

void leadingZeros( int value, int width) {            // display result with leading characters
  char valueStr[6];                                   // large enough to hold an int
  itoa (value, valueStr, 10);                         // itoa converts int to string
  int len = strlen(valueStr);                         // calculate length of valueStr
  if (len < width) {
    len = width - len;
    while (len--)
      lcd.print(' ');                                 // for leading zeros place '0' between (), for leading spaces place ' ' between ()
  }
  lcd.print(valueStr);
}
